# Fritzing sketch circuit12~16Vto12V (saved by Fritzing 0.9.3b)
breadboards: 1

parts:
  R1 = Resistor [tolerance=±5% resistance=220 package=THT]
  METER1 = 7-Segment Panel Voltmeter
  C1 = Electrolytic Capacitor [capacitance=1µF package="100 mil [THT, electrolytic]"]
  D1 = Zener Diode [part_number=1N4732A breakdown_voltage=12.1V package="300 mil [THT]"]

nets:
  N1: R1.Pin_0, METER1.V+, METER1.V-
  N2: R1.Pin_1, C1.+, D1.cathode
  N3: C1.-, D1.anode

notes:
  上排輸入 12V~16V
  下排約 11~12V
  簡易 12V~16V 轉 11.X~12.X V
  By 羽山 https://3wa.tw
  470㎌/ 50V
  220Ω
  Zener 12.1V

custom parts:
  7-Segment Panel Voltmeter: 7-Segment Panel Voltmeter (4.5 - 30V)
